// Logisim project logic_test.circ as structural Verilog
module main (
  input  a,
  input  b,
  input  c,
  input  d,
  output out1,
  output out2
);

  logic_test logic_test_1 (.a(a), .b(b), .c(c), .d(d), .out1(out1), .out2(out2));
endmodule

// VHDL entity logic_test, as the project stores it:
--library and package
library ieee;
use ieee.std_logic_1164.all;
use ieee.std_logic_arith.all;
use ieee.std_logic_unsigned.all;

--entity
entity logic_test is
	port(
		a,b,c,d :in std_logic;
		out1,out2 :out std_logic
	);
end entity logic_test;

--architecture
architecture bhv of logic_test is
begin
	out1 <= a and b and c and d;
	out2 <= a or b or c or d;
end architecture bhv;
